// Digital circuit Minicpu.dig as structural Verilog
module Minicpu (
  input  [7:0] M,
  input  [7:0] N,
  input  [13:0] progIn,
  input  progLoad,
  input  start,
  input  result,
  input  clk,
  input  reset,
  output valid,
  output done,
  output [7:0] \output ,
  output EQ
);

  wire _0, _1, _2, _3, _4, _5, _6, _7, _8, _9, _10, _11, _12, _13, _14, _15, _16, _17, _18, _19, _20, _21,
       _22, _23, _24, _25, _26, _27, _28, _29, _30, _31, _32, _33, _34, _35, _36, _37, _38, _39, _40, _41,
       _42, _43, _44, _45, _46, _47, _48, _49, _50, _51, _52, _53, _54, _55, _56, _57, _58, _59, _60, _61,
       _62, AfterExecute, and_1_out, and_2_out, and_3_out, and_4_out, and_5_out, and_6_out, and_7_out,
       and_8_out, and_11_out, and_12_out, and_13_out, and_14_out, and_15_out, and_16_out, and_17_out,
       and_19_out, and_20_out, and_21_out, and_22_out, and_23_out, and_24_out, and_26_out, and_27_out,
       and_28_out, and_29_out, and_30_out, and_31_out, comparator_1_gt, comparator_2_eq, comparator_3_eq,
       comparator_3_gt, comparator_3_lt, comparator_4_eq, comparator_4_lt, comparator_5_eq, comparator_5_lt,
       comparator_6_eq, comparator_7_eq, comparator_7_lt, comparator_8_eq, comparator_8_gt, comparator_9_gt,
       done_q, ExecuteState, ExecuteState_plus, FacCal, FacCal_plus, FacLoad, FacLoad_plus, FacSendA,
       FacSendA_plus, FacSendB, FacSendB_plus, FetchState, FetchState_plus, GTflag, IdleState,
       IdleState_plus, IsPrimeALU, LCMState, LCMState_plus, LoadState, LoadState_plus, LTflag, MaxFind,
       MaxFind_plus, MaxLoad, MaxLoad_plus, MaxSend, MaxSend_plus, multiplexer_18_out, multiplexer_19_out,
       multiplexer_20_out, multiplexer_22_out, multiplexer_24_out, multiplexer_25_out, multiplexer_26_out,
       multiplexer_34_out, multiplexer_35_out, multiplexer_51_out, not_1_out, not_2_out, not_3_out,
       not_4_out, not_5_out, not_6_out, not_7_out, not_8_out, not_9_out, or_1_out, or_2_out, or_3_out,
       or_4_out, or_5_out, or_6_out, or_7_out, or_8_out, or_9_out, or_10_out, or_11_out, or_12_out,
       or_13_out, or_14_out, or_15_out, or_16_out, or_17_out, or_19_out, or_20_out, or_21_out, or_22_out,
       or_23_out, or_24_out, or_25_out, or_27_out, or_28_out, or_29_out, or_30_out, or_31_out, or_32_out,
       or_33_out, or_35_out, or_36_out, or_37_out, or_38_out, or_39_out, or_40_out, Q_fa, Q_fb, Q_LCM,
       Q_LCM_plus, Q_ma, Q_mb, Qa, Qa_plus, Qb, Qb_plus, Qc, Qc_plus, ResetState, ResetState_plus, SendState,
       SendState_plus, STOP_CODE, StopFacCal, StopFindMax, StopReset, StopSend, WaitState, WaitState_plus;
  wire [1:0] and_9_out, and_33_out;
  wire [7:0] accA, accB, add_1_s, add_2_s, add_3_s, add_4_s, AddALU, adrMax, AndALU, Data_out, div_1_r,
       DivALU, LftLogALU, LftRotALU, LoadCount, ModALU, MulALU, multiplexer_1_out, multiplexer_2_out,
       multiplexer_3_out, multiplexer_4_out, multiplexer_5_out, multiplexer_7_out, multiplexer_9_out,
       multiplexer_10_out, multiplexer_11_out, multiplexer_16_out, multiplexer_17_out, multiplexer_21_out,
       multiplexer_23_out, multiplexer_28_out, multiplexer_29_out, multiplexer_30_out, multiplexer_31_out,
       multiplexer_32_out, multiplexer_33_out, multiplexer_36_out, multiplexer_38_out, multiplexer_40_out,
       multiplexer_41_out, multiplexer_42_out, multiplexer_43_out, multiplexer_44_out, multiplexer_45_out,
       multiplexer_47_out, multiplexer_48_out, multiplexer_49_out, multiplexer_50_out, multiplexer_53_out,
       multiplexer_54_out, multiplexer_55_out, multiplexer_56_out, multiplexer_57_out, multiplexer_58_out,
       NotALU, notconnected_1_out, notconnected_2_out, notconnected_3_out, notconnected_4_out,
       notconnected_5_out, notconnected_6_out, notconnected_7_out, notconnected_8_out, notconnected_9_out,
       notconnected_10_out, notconnected_11_out, notconnected_12_out, notconnected_13_out,
       notconnected_14_out, notconnected_15_out, notconnected_16_out, notconnected_17_out,
       notconnected_18_out, notconnected_19_out, notconnected_20_out, notconnected_21_out,
       notconnected_22_out, notconnected_23_out, notconnected_24_out, notconnected_25_out,
       notconnected_26_out, notconnected_27_out, notconnected_28_out, OrALU, PC, PowALU, pRAM_out, regC,
       regD, regMax, ResetAddress, RgtLogALU, RgtRotALU, rRAM_out, SendCount, SubALU, XorALU;
  wire [13:0] inMax, IR_out;
  wire [13:8] pRAM_d1;
  wire [15:0] accFac, LCM_Rom_d, mul_1_mul, multiplexer_8_out, multiplexer_12_out, multiplexer_13_out,
       multiplexer_14_out, multiplexer_15_out, regFac, RegLCM, sub_1_s, sub_2_s;
  wire [31:16] mul_1_mul_2;

  Add #(.Bits(8)) add_1 (.a(PC), .b(8'h1), .c_i(1'b0), .s(add_1_s));  // open: c_o
  or or_1 (or_1_out, _18, _19, _20, _21, _22, _23);
  Multiplexer #(.Bits(8)) multiplexer_1 (
    .sel(and_1_out), .in_0(add_1_s), .in_1(multiplexer_3_out), .out(multiplexer_1_out));
  and and_1 (and_1_out, ExecuteState_plus, or_1_out);
  Multiplexer #(.Bits(8)) multiplexer_2 (
    .sel(or_4_out), .in_0(multiplexer_1_out), .in_1({8{1'b0}}), .out(multiplexer_2_out));
  Multiplexer #(.Selector_Bits(3), .Bits(8)) multiplexer_3 (
    .sel(Data_out[2:0]), .in_0(IR_out[7:0]), .in_1(multiplexer_11_out), .in_2(multiplexer_10_out),
    .in_3(multiplexer_9_out), .in_4(multiplexer_5_out), .in_5(multiplexer_4_out), .in_6(multiplexer_7_out),
    .in_7(notconnected_1_out), .out(multiplexer_3_out));
  or or_2 (or_2_out, EQ, LTflag);
  Multiplexer #(.Bits(8)) multiplexer_4 (.sel(or_2_out), .in_0(PC), .in_1(IR_out[7:0]), .out(multiplexer_4_out));
  or or_3 (or_3_out, ResetState_plus, ResetState, FetchState, and_1_out);
  or or_4 (or_4_out, ResetState_plus, ResetState);
  // NotConnected on notconnected_1_out
  Comparator #(.Bits(8)) comparator_1 (.a(rRAM_out), .b(\output ), .gt(comparator_1_gt));  // open: eq, lt
  Multiplexer #(.Bits(8)) multiplexer_5 (.sel(or_5_out), .in_0(add_1_s), .in_1(IR_out[7:0]), .out(multiplexer_5_out));
  Multiplexer #(.Bits(8)) multiplexer_6 (
    .sel(comparator_1_gt), .in_0(rRAM_out), .in_1(\output ), .out(multiplexer_8_out[7:0]));
  Multiplexer #(.Bits(8)) multiplexer_7 (.sel(or_6_out), .in_0(add_1_s), .in_1(IR_out[7:0]), .out(multiplexer_7_out));
  ROM #(.AddrBits(8)) rom_1 (.A(accA), .sel(1'b1), .D(IsPrimeALU));
  Multiplexer #(.Bits(8)) multiplexer_8 (
    .sel(comparator_1_gt), .in_0(\output ), .in_1(rRAM_out), .out(multiplexer_8_out[15:8]));
  Register #(.Bits(8)) u_PC (.D(multiplexer_2_out), .C(clk), .en(or_3_out), .Q(PC));
  or or_5 (or_5_out, EQ, GTflag);
  Multiplexer #(.Bits(8)) multiplexer_9 (.sel(LTflag), .in_0(add_1_s), .in_1(IR_out[7:0]), .out(multiplexer_9_out));
  and and_2 (and_2_out, clk, ExecuteState_plus);
  or or_6 (or_6_out, EQ, LTflag);
  Multiplexer #(.Bits(8)) multiplexer_10 (.sel(GTflag), .in_0(add_1_s), .in_1(IR_out[7:0]), .out(multiplexer_10_out));
  and and_3 (and_3_out, StopFacCal, FacCal);
  and and_4 (and_4_out, ~StopFacCal, FacCal);  // And
  ROM #(.AddrBits(16), .Bits(16)) LCM_Rom (.A(multiplexer_8_out), .sel(1'b1), .D(LCM_Rom_d));
  Multiplexer #(.Bits(8)) multiplexer_11 (.sel(EQ), .in_0(add_1_s), .in_1(IR_out[7:0]), .out(multiplexer_11_out));
  or or_7 (or_7_out, FacSendA, and_3_out);
  or or_8 (or_8_out, and_4_out, FacSendA, FacLoad);
  ROM #(.AddrBits(6), .Bits(8)) rom_2 (.A({accA[2:0], accB[2:0]}), .sel(1'b1), .D(PowALU));
  Register #(.Bits(16)) u_RegLCM (.D(LCM_Rom_d), .C(and_2_out), .en(ExecuteState_plus), .Q(RegLCM));
  Mul #(.Bits(16)) mul_1 (.a(accFac), .b(regFac), .mul({mul_1_mul_2, mul_1_mul}));
  and and_5 (and_5_out, MaxLoad_plus, FetchState);
  and and_6 (and_6_out, or_7_out, ExecuteState_plus, _52);
  and and_7 (and_7_out, ExecuteState_plus, _52, or_8_out);
  Comparator #(.Bits(16)) comparator_2 (
    .a({{13{1'b0}}, accA[2:0]}), .b({16{1'b0}}), .eq(comparator_2_eq));  // open: gt, lt
  Sub #(.Bits(16)) sub_1 (.a({{13{1'b0}}, accA[2:0]}), .b(16'h1), .c_i(1'b0), .s(sub_1_s));  // open: c_o
  Multiplexer #(.Bits(16)) multiplexer_12 (
    .sel(comparator_2_eq), .in_0(mul_1_mul), .in_1(16'h1), .out(multiplexer_12_out));
  or or_9 (or_9_out, and_5_out, MaxFind_plus);
  Sub #(.Bits(16)) sub_2 (.a(regFac), .b(16'h1), .c_i(1'b0), .s(sub_2_s));  // open: c_o
  Multiplexer #(.Bits(16)) multiplexer_13 (
    .sel(comparator_2_eq), .in_0(sub_2_s), .in_1(16'h1), .out(multiplexer_13_out));
  and and_8 (and_8_out, _53, or_9_out);
  and and_9 (and_9_out[1], ~FetchState, and_6_out);  // And
  and and_10 (and_9_out[0], ~FetchState, and_7_out);  // And
  Multiplexer #(.Bits(16)) multiplexer_14 (
    .sel(FacLoad_plus), .in_0(multiplexer_12_out), .in_1({{13{1'b0}}, accA[2:0]}), .out(multiplexer_14_out));
  Multiplexer #(.Bits(16)) multiplexer_15 (
    .sel(FacLoad_plus), .in_0(multiplexer_13_out), .in_1(sub_1_s), .out(multiplexer_15_out));
  and and_11 (and_11_out, and_8_out, ExecuteState_plus);
  and and_12 (and_12_out, _48, ExecuteState_plus);
  Multiplexer #(.Bits(8)) multiplexer_16 (
    .sel(LoadState_plus), .in_0(IR_out[7:0]), .in_1(LoadCount), .out(multiplexer_16_out));
  Comparator #(.Signed("true"), .Bits(8)) comparator_3 (
    .a(accA), .b(accB), .gt(comparator_3_gt), .eq(comparator_3_eq), .lt(comparator_3_lt));
  LED led_1 (.in(Qa_plus));
  or or_10 (or_10_out, FacCal_plus, FacLoad_plus);
  or or_11 (or_11_out, FacCal_plus, FacLoad_plus);
  Multiplexer #(.Bits(8)) multiplexer_17 (.sel(and_11_out), .in_0(PC), .in_1(adrMax), .out(multiplexer_17_out));
  or or_12 (or_12_out, and_12_out, ResetState_plus);
  LED led_2 (.in(Qb_plus));
  LED led_3 (.in(Qc_plus));
  or or_13 (or_13_out, _1, _3, _6, _8, _14, _15, _16, _32, _33, _34, _35, _36, _37, _40, _41, _42, _43, _44, _45, _46, _47);
  D_FF d_ff_1 (.D(and_9_out[1]), .C(clk), .Q(Q_fa));  // open: nQ
  D_FF d_ff_2 (.D(and_9_out[0]), .C(clk), .Q(Q_fb));  // open: nQ
  Decoder #(.Selector_Bits(2)) decoder_1 (
    .sel(and_9_out), .out_0(FacLoad_plus), .out_1(FacCal_plus), .out_2(FacSendA_plus), .out_3(FacSendB_plus));
  RAMDualAccess #(.AddrBits(8), .Bits(14)) pRAM (
    .str(LoadState_plus), .C(clk), .ld(_15), .A1(multiplexer_16_out), .Din1(progIn), .A2(multiplexer_17_out),
    .D1({pRAM_d1, pRAM_out}), .D2(inMax));
  Multiplexer multiplexer_18 (.sel(ResetState_plus), .in_0(comparator_3_lt), .in_1(1'b0), .out(multiplexer_18_out));
  and and_13 (and_13_out, ~IdleState_plus, IdleState);  // And
  and and_14 (and_14_out, or_13_out, ExecuteState_plus);
  not not_1 (not_1_out, AfterExecute);
  Register #(.Bits(16)) u_accFac (.D(multiplexer_14_out), .C(clk), .en(or_10_out), .Q(accFac));
  Register #(.Bits(16)) u_regFac (.D(multiplexer_15_out), .C(clk), .en(or_11_out), .Q(regFac));
  Multiplexer multiplexer_19 (.sel(_51), .in_0(not_1_out), .in_1(1'b1), .out(multiplexer_19_out));
  Multiplexer multiplexer_20 (.sel(ResetState_plus), .in_0(comparator_3_gt), .in_1(1'b0), .out(multiplexer_20_out));
  Multiplexer #(.Bits(8)) multiplexer_21 (.sel(_14), .in_0(Data_out), .in_1(regC), .out(multiplexer_21_out));
  Decoder #(.Selector_Bits(2)) decoder_2 (
    .sel({Q_fa, Q_fb}), .out_0(FacLoad), .out_1(FacCal), .out_2(FacSendA), .out_3(FacSendB));
  Comparator #(.Bits(16)) comparator_4 (.a(regFac), .b(16'h1), .eq(comparator_4_eq), .lt(comparator_4_lt));  // open: gt
  Multiplexer multiplexer_22 (.sel(_49), .in_0(comparator_3_eq), .in_1(IsPrimeALU), .out(multiplexer_22_out));
  Register GT (.D(multiplexer_20_out), .C(clk), .en(or_12_out), .Q(GTflag));
  Register LT (.D(multiplexer_18_out), .C(clk), .en(or_12_out), .Q(LTflag));
  or or_14 (or_14_out, StopSend, ResetState_plus, and_13_out);
  and and_15 (and_15_out, valid, IdleState_plus);
  or or_15 (or_15_out, WaitState_plus, ResetState_plus, IdleState_plus);
  Multiplexer #(.Bits(8)) multiplexer_23 (
    .sel(ResetState_plus), .in_0(multiplexer_21_out), .in_1({8{1'b0}}), .out(multiplexer_23_out));
  or or_16 (or_16_out, and_14_out, ResetState_plus);
  and and_16 (and_16_out, result, valid);
  not not_2 (not_2_out, StopSend);
  not not_3 (not_3_out, Q_LCM);
  Comparator #(.Bits(16)) comparator_5 (.a(accFac), .b(16'h1), .eq(comparator_5_eq), .lt(comparator_5_lt));  // open: gt
  not not_4 (not_4_out, StopSend);
  Register #(.Bits(8)) u_accA (.D(multiplexer_23_out), .C(clk), .en(or_16_out), .Q(accA));
  Multiplexer #(.Selector_Bits(3)) multiplexer_24 (
    .sel({Qa, Qb, Qc}), .in_0(and_16_out), .in_1(1'b0), .in_2(1'b0), .in_3(1'b1), .in_4(multiplexer_19_out),
    .in_5(1'b1), .in_6(not_2_out), .in_7(not_3_out), .out(multiplexer_24_out));
  Comparator #(.Bits(8)) comparator_6 (.a(div_1_r), .b({8{1'b0}}), .eq(comparator_6_eq));  // open: gt, lt
  Multiplexer multiplexer_25 (.sel(_50), .in_0(multiplexer_22_out), .in_1(comparator_6_eq), .out(multiplexer_25_out));
  Multiplexer multiplexer_26 (.sel(ResetState_plus), .in_0(multiplexer_25_out), .in_1(1'b0), .out(multiplexer_26_out));
  Register u_done (.D(not_4_out), .C(clk), .en(or_14_out), .Q(done_q));
  or or_17 (or_17_out, and_15_out, WaitState_plus);
  Multiplexer multiplexer_27 (.sel(and_19_out), .in_0(multiplexer_24_out), .in_1(1'b0), .out(Qa_plus));
  or or_18 (StopFacCal, comparator_5_lt, comparator_5_eq, comparator_4_eq, comparator_4_lt);
  Register u_EQ (.D(multiplexer_26_out), .C(clk), .en(or_19_out), .Q(EQ));
  or or_19 (or_19_out, and_17_out, ResetState_plus);
  not not_5 (not_5_out, done_q);
  not not_6 (not_6_out, SendState);
  Register u_valid (.D(or_17_out), .C(clk), .en(or_15_out), .Q(valid));
  Div #(.Bits(8)) div_1 (.a({1'b0, accA[6:0]}), .b({1'b0, accB[6:0]}), .r(div_1_r));  // open: q
  and and_17 (and_17_out, or_21_out, ExecuteState_plus);
  and and_18 (done, not_5_out, not_6_out);
  D_FF u_Qa (.D(Qa_plus), .C(clk), .Q(Qa));  // open: nQ
  and and_19 (and_19_out, ~ResetState, reset);  // And
  or or_20 (or_20_out, _5, _9, _10, _13);
  or or_21 (or_21_out, _50, _49, _48);
  and and_20 (and_20_out, or_20_out, ExecuteState_plus);
  Multiplexer #(.Bits(8)) multiplexer_28 (.sel(FacSendA_plus), .in_0(8'hb), .in_1(8'ha), .out(multiplexer_28_out));
  Multiplexer #(.Bits(8)) multiplexer_29 (
    .sel(_51), .in_0(IR_out[7:0]), .in_1({4'b0000, IR_out[3:0]}), .out(multiplexer_29_out));
  Multiplexer #(.Bits(8)) multiplexer_30 (.sel(Q_LCM_plus), .in_0(8'he), .in_1(8'hf), .out(multiplexer_30_out));
  Multiplexer #(.Bits(8)) multiplexer_31 (.sel(_13), .in_0(Data_out), .in_1(M), .out(multiplexer_31_out));
  Multiplexer #(.Bits(8)) multiplexer_32 (
    .sel(LCMState_plus), .in_0(multiplexer_29_out), .in_1(multiplexer_30_out), .out(multiplexer_32_out));
  not not_7 (not_7_out, ResetState);
  Multiplexer #(.Bits(8)) multiplexer_33 (
    .sel(ResetState_plus), .in_0(multiplexer_31_out), .in_1({8{1'b0}}), .out(multiplexer_33_out));
  or or_22 (or_22_out, and_20_out, ResetState_plus);
  or or_23 (or_23_out, progLoad, start, result);
  or or_24 (or_24_out, progLoad, start);
  and and_21 (and_21_out, _51, LCMState_plus);
  and and_22 (and_22_out, _17, ExecuteState_plus);
  Counter #(.Bits(8)) counter_1 (.en(ResetState), .C(clk), .clr(not_7_out), .out(ResetAddress));  // open: ovf
  Register #(.Bits(8)) u_regC (.D(multiplexer_33_out), .C(clk), .en(or_22_out), .Q(regC));
  not not_8 (not_8_out, StopSend);
  Comparator #(.Bits(8)) comparator_7 (
    .a(ResetAddress), .b(8'hf), .eq(comparator_7_eq), .lt(comparator_7_lt));  // open: gt
  Multiplexer #(.Selector_Bits(3)) multiplexer_34 (
    .sel({Qa, Qb, Qc}), .in_0(or_23_out), .in_1(1'b0), .in_2(or_24_out), .in_3(1'b0), .in_4(AfterExecute),
    .in_5(result), .in_6(not_8_out), .in_7(1'b1), .out(multiplexer_34_out));
  Multiplexer multiplexer_35 (.sel(_52), .in_0(1'b1), .in_1(FacSendB), .out(multiplexer_35_out));
  Register #(.Bits(14)) IR (.D(inMax), .C(clk), .en(FetchState_plus), .Q(IR_out));
  or or_25 (or_25_out, and_21_out, and_22_out);
  Multiplexer #(.Bits(8)) multiplexer_36 (
    .sel(_52), .in_0(multiplexer_32_out), .in_1(multiplexer_28_out), .out(multiplexer_36_out));
  or or_26 (StopReset, comparator_7_eq, comparator_7_lt);
  Multiplexer multiplexer_37 (.sel(and_23_out), .in_0(multiplexer_34_out), .in_1(1'b0), .out(Qb_plus));
  Multiplexer #(.Bits(8)) multiplexer_38 (.sel(_53), .in_0(multiplexer_36_out), .in_1(8'h9), .out(multiplexer_38_out));
  Multiplexer multiplexer_39 (.sel(_53), .in_0(multiplexer_35_out), .in_1(MaxSend), .out(AfterExecute));
  or or_27 (or_27_out, FacSendB_plus, FacSendA_plus);
  or or_28 (or_28_out, MaxSend_plus, or_27_out, or_25_out);
  or or_29 (or_29_out, or_28_out, ResetState_plus);
  Multiplexer #(.Bits(8)) multiplexer_40 (
    .sel(ResetState_plus), .in_0(multiplexer_38_out), .in_1(ResetAddress), .out(multiplexer_40_out));
  or or_30 (or_30_out, _2, _4, _14);
  D_FF u_Qb (.D(Qb_plus), .C(clk), .Q(Qb));  // open: nQ
  and and_23 (and_23_out, ~ResetState, reset);  // And
  and and_24 (and_24_out, or_30_out, ExecuteState_plus);
  Multiplexer #(.Bits(8)) multiplexer_41 (
    .sel(LCMState_plus), .in_0(Data_out), .in_1(multiplexer_42_out), .out(multiplexer_41_out));
  Multiplexer #(.Bits(8)) multiplexer_42 (
    .sel(Q_LCM_plus), .in_0(RegLCM[15:8]), .in_1(RegLCM[7:0]), .out(multiplexer_42_out));
  Multiplexer #(.Bits(8)) multiplexer_43 (.sel(_14), .in_0(Data_out), .in_1(regD), .out(multiplexer_43_out));
  Decoder #(.Selector_Bits(6)) decoder_3 (
    .sel(IR_out[13:8]), .out_0(_0), .out_1(_1), .out_2(_2), .out_3(_3), .out_4(_4), .out_5(_5), .out_6(_6),
    .out_7(_7), .out_8(_8), .out_9(_9), .out_10(_10), .out_11(_11), .out_12(_12), .out_13(_13), .out_14(_14),
    .out_15(_15), .out_16(_16), .out_17(_17), .out_18(_18), .out_19(_19), .out_20(_20), .out_21(_21),
    .out_22(_22), .out_23(_23), .out_24(_24), .out_25(_25), .out_26(_26), .out_27(_27), .out_28(_28),
    .out_29(_29), .out_30(_30), .out_31(_31), .out_32(_32), .out_33(_33), .out_34(_34), .out_35(_35),
    .out_36(_36), .out_37(_37), .out_38(_38), .out_39(_39), .out_40(_40), .out_41(_41), .out_42(_42),
    .out_43(_43), .out_44(_44), .out_45(_45), .out_46(_46), .out_47(_47), .out_48(_48), .out_49(_49),
    .out_50(_50), .out_51(_51), .out_52(_52), .out_53(_53), .out_54(_54), .out_55(_55), .out_56(_56),
    .out_57(_57), .out_58(_58), .out_59(_59), .out_60(_60), .out_61(_61), .out_62(_62), .out_63(STOP_CODE));
  or or_31 (or_31_out, _16, _51);
  Multiplexer #(.Bits(8)) multiplexer_44 (
    .sel(ResetState_plus), .in_0(multiplexer_43_out), .in_1({8{1'b0}}), .out(multiplexer_44_out));
  or or_32 (or_32_out, and_24_out, ResetState_plus);
  Multiplexer #(.Bits(8)) multiplexer_45 (
    .sel(ResetState_plus), .in_0(multiplexer_49_out), .in_1({8{1'b0}}), .out(multiplexer_45_out));
  and and_25 (Q_LCM_plus, ~Q_LCM, LCMState);  // And
  Register #(.Bits(8)) u_accB (.D(multiplexer_44_out), .C(clk), .en(or_32_out), .Q(accB));
  // NotConnected on notconnected_2_out
  // NotConnected on notconnected_3_out
  // NotConnected on notconnected_4_out
  // NotConnected on notconnected_5_out
  // NotConnected on notconnected_6_out
  // NotConnected on notconnected_7_out
  // NotConnected on notconnected_8_out
  // NotConnected on notconnected_9_out
  // NotConnected on notconnected_10_out
  // NotConnected on notconnected_11_out
  // NotConnected on notconnected_12_out
  // NotConnected on notconnected_13_out
  // NotConnected on notconnected_14_out
  // NotConnected on notconnected_15_out
  // NotConnected on notconnected_16_out
  // NotConnected on notconnected_17_out
  // NotConnected on notconnected_18_out
  // NotConnected on notconnected_19_out
  // NotConnected on notconnected_20_out
  // NotConnected on notconnected_21_out
  // NotConnected on notconnected_22_out
  // NotConnected on notconnected_23_out
  // NotConnected on notconnected_24_out
  // NotConnected on notconnected_25_out
  // NotConnected on notconnected_26_out
  // NotConnected on notconnected_27_out
  Multiplexer #(.Selector_Bits(6), .Bits(8)) multiplexer_46 (
    .sel(IR_out[13:8]), .in_0(notconnected_28_out), .in_1(IR_out[7:0]), .in_2(IR_out[7:0]), .in_3(accB),
    .in_4(accA), .in_5(accA), .in_6(regC), .in_7(accA), .in_8(regD), .in_9(M), .in_10(N), .in_11(M),
    .in_12(N), .in_13(notconnected_27_out), .in_14(notconnected_26_out), .in_15(pRAM_out), .in_16(rRAM_out),
    .in_17(accA), .in_18({8{1'b0}}), .in_19(8'h1), .in_20(8'h2), .in_21(8'h3), .in_22(8'h4), .in_23(8'h5),
    .in_24(8'h6), .in_25(notconnected_25_out), .in_26(notconnected_24_out), .in_27(notconnected_23_out),
    .in_28(notconnected_22_out), .in_29(notconnected_21_out), .in_30(notconnected_20_out),
    .in_31(notconnected_19_out), .in_32(AddALU), .in_33(SubALU), .in_34(MulALU), .in_35(DivALU),
    .in_36(ModALU), .in_37(PowALU), .in_38(notconnected_18_out), .in_39(notconnected_17_out), .in_40(NotALU),
    .in_41(AndALU), .in_42(OrALU), .in_43(XorALU), .in_44(LftLogALU), .in_45(LftRotALU), .in_46(RgtLogALU),
    .in_47(RgtRotALU), .in_48(notconnected_16_out), .in_49(notconnected_15_out), .in_50(notconnected_14_out),
    .in_51(multiplexer_53_out), .in_52(notconnected_13_out), .in_53(notconnected_12_out),
    .in_54(notconnected_11_out), .in_55(notconnected_10_out), .in_56(notconnected_9_out),
    .in_57(notconnected_8_out), .in_58(notconnected_7_out), .in_59(notconnected_6_out),
    .in_60(notconnected_5_out), .in_61(notconnected_4_out), .in_62(notconnected_3_out),
    .in_63(notconnected_2_out), .out(Data_out));
  // NotConnected on notconnected_28_out
  RAMDualAccess #(.AddrBits(8), .Bits(8)) rRAM (
    .str(or_29_out), .C(clk), .ld(or_31_out), .A1(multiplexer_40_out), .Din1(multiplexer_45_out),
    .A2(multiplexer_47_out), .D1(rRAM_out), .D2(\output ));
  Multiplexer #(.Bits(8)) multiplexer_47 (
    .sel(_51), .in_0(SendCount), .in_1({4'b0000, IR_out[7:4]}), .out(multiplexer_47_out));
  Multiplexer #(.Bits(8)) multiplexer_48 (
    .sel(_52), .in_0(multiplexer_41_out), .in_1(multiplexer_50_out), .out(multiplexer_48_out));
  Comparator #(.Bits(8)) comparator_8 (
    .a(SendCount), .b(8'hf), .gt(comparator_8_gt), .eq(comparator_8_eq));  // open: lt
  or or_33 (or_33_out, reset, start);
  not not_9 (not_9_out, result);
  Multiplexer #(.Bits(8)) multiplexer_49 (
    .sel(_53), .in_0(multiplexer_48_out), .in_1(regMax), .out(multiplexer_49_out));
  Multiplexer #(.Bits(8)) multiplexer_50 (
    .sel(FacSendA_plus), .in_0(accFac[7:0]), .in_1(accFac[15:8]), .out(multiplexer_50_out));
  or or_34 (StopSend, comparator_8_gt, comparator_8_eq);
  D_FF LCM_Sub (.D(Q_LCM_plus), .C(clk), .Q(Q_LCM));  // open: nQ
  Multiplexer #(.Selector_Bits(3)) multiplexer_51 (
    .sel({Qa, Qb, Qc}), .in_0(or_33_out), .in_1(StopReset), .in_2(start), .in_3(STOP_CODE),
    .in_4(AfterExecute), .in_5(not_9_out), .in_6(1'b0), .in_7(1'b1), .out(multiplexer_51_out));
  Multiplexer multiplexer_52 (.sel(and_26_out), .in_0(multiplexer_51_out), .in_1(1'b1), .out(Qc_plus));
  LED led_4 (.in(MaxLoad_plus));
  LED led_5 (.in(MaxFind_plus));
  LED led_6 (.in(MaxSend_plus));
  Multiplexer #(.Bits(8)) multiplexer_53 (
    .sel(Q_LCM_plus), .in_0(RegLCM[15:8]), .in_1(RegLCM[7:0]), .out(multiplexer_53_out));
  Seven_Seg_Hex seven_seg_hex_1 (.d(\output [7:4]), .dp(1'b0));
  or or_35 (or_35_out, _7, _11, _12, _13);
  D_FF u_Qc (.D(Qc_plus), .C(clk), .Q(Qc));  // open: nQ
  and and_26 (and_26_out, ~ResetState, reset);  // And
  and and_27 (and_27_out, or_35_out, ExecuteState_plus);
  Seven_Seg_Hex seven_seg_hex_2 (.d(\output [3:0]), .dp(1'b0));
  Decoder #(.Selector_Bits(3)) decoder_4 (
    .sel({Qa_plus, Qb_plus, Qc_plus}), .out_0(IdleState_plus), .out_1(ResetState_plus),
    .out_2(LoadState_plus), .out_3(FetchState_plus), .out_4(ExecuteState_plus), .out_5(WaitState_plus),
    .out_6(SendState_plus), .out_7(LCMState_plus));
  Counter #(.Bits(8)) counter_2 (.en(SendState), .C(clk), .clr(~SendState), .out(SendCount));  // open: ovf
  Counter #(.Bits(8)) counter_3 (.en(LoadState_plus), .C(clk), .clr(~LoadState_plus), .out(LoadCount));  // open: ovf
  Multiplexer #(.Bits(8)) multiplexer_54 (.sel(_13), .in_0(Data_out), .in_1(N), .out(multiplexer_54_out));
  Multiplexer #(.Bits(8)) multiplexer_55 (
    .sel(ResetState_plus), .in_0(multiplexer_54_out), .in_1({8{1'b0}}), .out(multiplexer_55_out));
  Register #(.Bits(8)) u_regD (.D(multiplexer_55_out), .C(clk), .en(or_36_out), .Q(regD));
  or or_36 (or_36_out, and_27_out, ResetState_plus);
  Decoder #(.Selector_Bits(3)) decoder_5 (
    .sel({Qa, Qb, Qc}), .out_0(IdleState), .out_1(ResetState), .out_2(LoadState), .out_3(FetchState),
    .out_4(ExecuteState), .out_5(WaitState), .out_6(SendState), .out_7(LCMState));
  or or_37 (or_37_out, MaxFind, MaxLoad);
  and and_28 (and_28_out, MaxFind, ~StopFindMax);  // And
  or or_38 (or_38_out, MaxLoad, and_28_out);
  Add #(.Bits(8)) add_2 (.a(adrMax), .b(8'h1), .c_i(1'b0), .s(add_2_s));  // open: c_o
  and and_29 (and_29_out, ExecuteState, ~FetchState_plus, _53);  // And
  and and_30 (and_30_out, or_37_out, StopFindMax, ExecuteState_plus, _53);
  and and_31 (and_31_out, ExecuteState_plus, _53, or_38_out);
  or or_39 (or_39_out, and_29_out, FetchState);
  Add #(.Bits(8)) add_3 (.a(inMax[7:0]), .b(8'h80), .c_i(1'b0), .s(add_3_s));  // open: c_o
  Add #(.Bits(8)) add_4 (.a(regMax), .b(8'h80), .c_i(1'b0), .s(add_4_s));  // open: c_o
  Multiplexer #(.Bits(8)) multiplexer_56 (.sel(FetchState), .in_0(add_2_s), .in_1(accA), .out(multiplexer_56_out));
  Add #(.Bits(8)) add_5 (.a(accA), .b(accB), .c_i(1'b0), .s(AddALU));  // open: c_o
  Sub #(.Bits(8)) sub_3 (.a(accA), .b(accB), .c_i(1'b0), .s(SubALU));  // open: c_o
  Mul #(.Bits(4)) mul_2 (.a(accA[3:0]), .b(accB[3:0]), .mul(MulALU));
  Div #(.Bits(8)) div_2 (.a(accA), .b(accB), .q(DivALU), .r(ModALU));
  Comparator #(.Bits(8)) comparator_9 (.a(add_3_s), .b(add_4_s), .gt(comparator_9_gt));  // open: eq, lt
  Register #(.Bits(8)) u_adrMax (.D(multiplexer_56_out), .C(~clk), .en(or_39_out), .Q(adrMax));
  Multiplexer #(.Bits(8)) multiplexer_57 (
    .sel(comparator_9_gt), .in_0(regMax), .in_1(inMax[7:0]), .out(multiplexer_57_out));
  and and_32 (and_33_out[1], and_30_out, ~FetchState);  // And
  and and_33 (and_33_out[0], ~FetchState, and_31_out);  // And
  or or_40 (or_40_out, MaxLoad_plus, MaxFind_plus);
  Multiplexer #(.Bits(8)) multiplexer_58 (
    .sel(MaxLoad_plus), .in_0(multiplexer_57_out), .in_1(inMax[7:0]), .out(multiplexer_58_out));
  Decoder #(.Selector_Bits(2)) decoder_6 (
    .sel(and_33_out), .out_0(MaxLoad_plus), .out_1(MaxFind_plus), .out_2(MaxSend_plus));  // open: out_3
  Comparator #(.Bits(8)) comparator_10 (.a(adrMax), .b(accB), .gt(StopFindMax));  // open: eq, lt
  assign NotALU = ~accA;  // Not not_10, 8 bits wide
  D_FF d_ff_3 (.D(and_33_out[1]), .C(clk), .Q(Q_ma));  // open: nQ
  D_FF d_ff_4 (.D(and_33_out[0]), .C(clk), .Q(Q_mb));  // open: nQ
  assign AndALU = accB & accA;  // And and_34, 8 bits wide
  assign OrALU = accB | accA;  // Or or_41, 8 bits wide
  assign XorALU = accB ^ accA;  // XOr xor_1, 8 bits wide
  Register #(.Bits(8)) u_regMax (.D(multiplexer_58_out), .C(clk), .en(or_40_out), .Q(regMax));
  Decoder #(.Selector_Bits(2)) decoder_7 (
    .sel({Q_ma, Q_mb}), .out_0(MaxLoad), .out_1(MaxFind), .out_2(MaxSend));  // open: out_3
  BarrelShifter #(.Bits(8)) barrelshifter_1 (.in(accA), .shift({1'b0, accB[2:0]}), .out(LftLogALU));
  BarrelShifter #(.Bits(8), .barrelShifterMode("rotate")) barrelshifter_2 (
    .in(accA), .shift({1'b0, accB[2:0]}), .out(LftRotALU));
  BarrelShifter #(.Bits(8), .direction("right")) barrelshifter_3 (
    .in(accA), .shift({1'b0, accB[2:0]}), .out(RgtLogALU));
  BarrelShifter #(.Bits(8), .barrelShifterMode("rotate"), .direction("right")) barrelshifter_4 (
    .in(accA), .shift({1'b0, accB[2:0]}), .out(RgtRotALU));

  // Other names for the same wires on the sheet: EQflag = EQ; IR_in[13:0] = inMax; Operand[7:0] = IR_out[7:0];
  //   StateMix[2:0] = {Qa, Qb, Qc}; State_plus_Mix[2:0] = {Qa_plus, Qb_plus, Qc_plus}; rRAM_out2[7:0] = \output 

  // Notes on the sheet:
  //   6833025121 คมสันต์ เผือกพิบูลย์
  //   Main contributor
  //   - ต่อ Opcode
  //   - ต่อ Data path
  //   - จัดการ done,valid,output
  //   - debug อื่นๆ
  //   6833115021 ธนิสรา สาทลาลัย
  //   - ออกแบบแต่ละ state
  //   - ช่วยต่อ state
  //   - debug state
  //   - debug อื่นๆ
  //   6833123021 ธีรภัทร ผลบุญ
  //   Main contributor
  //   - ช่วยออกแบบแต่ละ state
  //   - ต่อ state
  //   - implement reset
  //   - debug อื่นๆ
  //   - QA
  //   contents of rom_1 (hex, n*v repeats v):
  //   0,0,1,1,0,1,0,1,0,0,0,1,0,1,0,0,0,1,0,1,0,0,0,1,5*0,1,0,1,5*0
  //   ,1,0,0,0,1,0,1,0,0,0,1,5*0,1,5*0,1,0,1,5*0,1,0,0,0,1,0,1,5*0,1
  //   ,0,0,0,1,5*0,1,7*0,1,0,0,0,1,0,1,0,0,0,1,0,1,0,0,0,1,13*0,1,0,0,0
  //   ,1,5*0,1,0,1,9*0,1,0,1,5*0,1,5*0,1,0,0,0,1,5*0,1,5*0,1,0,1,9*0
  //   ,1,0,1,0,0,0,1,0,1,11*0,1,11*0,1,0,0,0,1,0,1,0,0,0,1,5*0,1,0,1
  //   ,9*0,1
  //   contents of LCM_Rom (hex, n*v repeats v):
  //   257*0,1,255*0,2,2,254*0,3,6,3,253*0,4,4,c,4,252*0,5,a,f,14,5,251*0
  //   ,6,6,6,c,1e,6,250*0,7,e,15,1c,23,2a,7,249*0,8,8,18,8,28,18,38
  //   ,8,248*0,9,12,9,24,2d,12,3f,48,9,247*0,a,a,1e,14,a,1e,46,28,5a
  //   ,a,246*0,b,16,21,2c,37,42,4d,58,63,6e,b,245*0,4*c,3c,c,54,18,24
  //   ,3c,84,c,244*0,d,1a,27,34,41,4e,5b,68,75,82,8f,9c,d,243*0,e,e
  //   ,2a,1c,46,2a,e,38,7e,46,9a,54,b6,e,242*0,f,1e,f,3c,f,1e,69,78
  //   ,2d,1e,a5,3c,c3,d2,f,241*0,10,10,30,10,50,30,70,10,90,50,b0,30
  //   ,d0,70,f0,10,240*0,11,22,33,44,55,66,77,88,99,aa,bb,cc,dd,ee,ff
  //   ,110,11,239*0,12,12,12,24,5a,12,7e,48,12,5a,c6,24,ea,7e,5a,90
  //   ,132,12,238*0,13,26,39,4c,5f,72,85,98,ab,be,d1,e4,f7,10a,11d,130
  //   ,143,156,13,237*0,14,14,3c,14,14,3c,8c,28,b4,14,dc,3c,104,8c,3c
  //   ,50,154,b4,17c,14,236*0,15,2a,15,54,69,2a,15,a8,3f,d2,e7,54,111
  //   ,2a,69,150,165,7e,18f,1a4,15,235*0,16,16,42,2c,6e,42,9a,58,c6
  //   ,6e,16,84,11e,9a,14a,b0,176,c6,1a2,dc,1ce,16,234*0,17,2e,45,5c
  //   ,73,8a,a1,b8,cf,e6,fd,114,12b,142,159,170,187,19e,1b5,1cc,1e3
  //   ,1fa,17,233*0,4*18,78,18,a8,18,48,78,108,18,138,a8,78,30,198,48
  //   ,1c8,78,a8,108,228,18,232*0,19,32,4b,64,19,96,af,c8,e1,32,113
  //   ,12c,145,15e,4b,190,1a9,1c2,1db,64,20d,226,23f,258,19,231*0,1a,1a
  //   ,4e,34,82,4e,b6,68,ea,82,11e,9c,1a,b6,186,d0,1ba,ea,1ee,104,222
  //   ,11e,256,138,28a,1a,230*0,1b,36,1b,6c,87,36,bd,d8,1b,10e,129,6c
  //   ,15f,17a,87,1b0,1cb,36,201,21c,bd,252,26d,d8,2a3,2be,1b,229*0
  //   ,1c,1c,54,1c,8c,54,1c,38,fc,8c,134,54,16c,1c,1a4,70,1dc,fc,214
  //   ,8c,54,134,284,a8,2bc,16c,2f4,1c,228*0,1d,3a,57,74,91,ae,cb,e8
  //   ,105,122,13f,15c,179,196,1b3,1d0,1ed,20a,227,244,261,27e,29b,2b8
  //   ,2d5,2f2,30f,32c,1d,227*0,1e,1e,1e,3c,1e,1e,d2,78,5a,1e,14a,3c
  //   ,186,d2,1e,f0,1fe,5a,23a,3c,d2,14a,2b2,78,96,186,10e,1a4,366,1e
  //   ,226*0,1f,3e,5d,7c,9b,ba,d9,f8,117,136,155,174,193,1b2,1d1,1f0
  //   ,20f,22e,24d,26c,28b,2aa,2c9,2e8,307,326,345,364,383,3a2,1f,225*0
  //   ,20,20,60,20,a0,60,e0,20,120,a0,160,60,1a0,e0,1e0,20,220,120,260
  //   ,a0,2a0,160,2e0,60,320,1a0,360,e0,3a0,1e0,3e0,20,224*0,21,42,21
  //   ,84,a5,42,e7,108,63,14a,21,84,1ad,1ce,a5,210,231,c6,273,294,e7
  //   ,42,2f7,108,339,35a,129,39c,3bd,14a,3ff,420,21,223*0,22,22,66
  //   ,44,aa,66,ee,88,132,aa,176,cc,1ba,ee,1fe,110,22,132,286,154,2ca
  //   ,176,30e,198,352,1ba,396,1dc,3da,1fe,41e,220,462,22,222*0,23,46
  //   ,69,8c,23,d2,23,118,13b,46,181,1a4,1c7,46,69,230,253,276,299,8c
  //   ,69,302,325,348,af,38e,3b1,8c,3f7,d2,43d,460,483,4a6,23,221*0
  //   ,4*24,b4,24,fc,48,24,b4,18c,24,1d4,fc,b4,90,264,24,2ac,b4,fc,18c
  //   ,33c,48,384,1d4,6c,fc,414,b4,45c,120,18c,264,4ec,24,220*0,25,4a
  //   ,6f,94,b9,de,103,128,14d,172,197,1bc,1e1,206,22b,250,275,29a,2bf
  //   ,2e4,309,32e,353,378,39d,3c2,3e7,40c,431,456,47b,4a0,4c5,4ea,50f
  //   ,534,25,219*0,26,26,72,4c,be,72,10a,98,156,be,1a2,e4,1ee,10a,23a
  //   ,130,286,156,26,17c,31e,1a2,36a,1c8,3b6,1ee,402,214,44e,23a,49a
  //   ,260,4e6,286,532,2ac,57e,26,218*0,27,4e,27,9c,c3,4e,111,138,75
  //   ,186,1ad,9c,27,222,c3,270,297,ea,2e5,30c,111,35a,381,138,3cf,4e
  //   ,15f,444,46b,186,4b9,4e0,1ad,52e,555,1d4,5a3,5ca,27,217*0,28,28
  //   ,78,28,28,78,118,28,168,28,1b8,78,208,118,78,50,2a8,168,2f8,28
  //   ,348,1b8,398,78,c8,208,438,118,488,78,4d8,a0,528,2a8,118,168,5c8
  //   ,2f8,618,28,216*0,29,52,7b,a4,cd,f6,11f,148,171,19a,1c3,1ec,215
  //   ,23e,267,290,2b9,2e2,30b,334,35d,386,3af,3d8,401,42a,453,47c,4a5
  //   ,4ce,4f7,520,549,572,59b,5c4,5ed,616,63f,668,29,215*0,2a,2a,2a
  //   ,54,d2,2a,2a,a8,7e,d2,1ce,54,222,2a,d2,150,2ca,7e,31e,1a4,2a,1ce
  //   ,3c6,a8,41a,222,17a,54,4c2,d2,516,2a0,1ce,2ca,d2,fc,612,31e,222
  //   ,348,6ba,2a,214*0,2b,56,81,ac,d7,102,12d,158,183,1ae,1d9,204,22f
  //   ,25a,285,2b0,2db,306,331,35c,387,3b2,3dd,408,433,45e,489,4b4,4df
  //   ,50a,535,560,58b,5b6,5e1,60c,637,662,68d,6b8,6e3,70e,2b,213*0
  //   ,2c,2c,84,2c,dc,84,134,58,18c,dc,2c,84,23c,134,294,b0,2ec,18c
  //   ,344,dc,39c,2c,3f4,108,44c,23c,4a4,134,4fc,294,554,160,84,2ec
  //   ,604,18c,65c,344,6b4,1b8,70c,39c,764,2c,212*0,2d,5a,2d,b4,2d,5a
  //   ,13b,168,2d,5a,1ef,b4,249,276,2d,2d0,2fd,5a,357,b4,13b,3de,40b
  //   ,168,e1,492,87,4ec,519,5a,573,5a0,1ef,5fa,13b,b4,681,6ae,249,168
  //   ,735,276,78f,7bc,2d,211*0,2e,2e,8a,5c,e6,8a,142,b8,19e,e6,1fa
  //   ,114,256,142,2b2,170,30e,19e,36a,1cc,3c6,1fa,2e,228,47e,256,4da
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  //   contents of rom_2 (hex, n*v repeats v):
  //   1,7*0,9*1,2,4,8,10,20,40,80,1,3,9,1b,51,f3,2d9,88b,1,4,10,40,100
  //   ,400,1000,4000,1,5,19,7d,271,c35,3d09,1312d,1,6,24,d8,510,1e60
  //   ,b640,44580,1,7,31,157,961,41a7,1cb91,c90f7
  //   Future 2
  //   Future 1
endmodule

/* Test case 01_P01T01:
M N progIn reset progLoad start result clk valid done output
0 0      0     0        0     0      0   0     x    x      x
0 0      0     0        0     0      0   1     x    x      x
0 0      0     1        0     0      0   0     x    x      x
0 0      0     1        0     0      0   1     0    0      x
0 0      0     0        0     0      0   0     0    0      x
0 0      0     0        0     0      0   1     0    0      x
0 0      0     0        0     0      0   0     0    0      x
0 0      0     0        0     0      0   1     0    0      x
0 0      0     0        0     0      0   0     0    0      x
0 0      0     0        0     0      0   1     0    0      x
0 0      0     0        0     0      0   0     0    0      x
0 0      0     0        0     0      0   1     0    0      x
0 0      0     0        0     0      0   0     0    0      x
0 0      0     0        0     0      0   1     0    0      x
0 0      0     0        0     0      0   0     0    0      x
0 0      0     0        0     0      0   1     0    0      x
0 0      0     0        0     0      0   0     0    0      x
0 0      0     0        0     0      0   1     0    0      x
0 0      0     0        0     0      0   0     0    0      x
0 0      0     0        0     0      0   1     0    0      x
0 0      0     0        0     0      0   0     0    0      x
0 0      0     0        0     0      0   1     0    0      x
0 0      0     0        0     0      0   0     0    0      x
0 0      0     0        0     0      0   1     0    0      x
0 0      0     0        0     0      0   0     0    0      x
0 0      0     0        0     0      0   1     0    0      x
0 0      0     0        0     0      0   0     0    0      x
0 0      0     0        0     0      0   1     0    0      x
0 0      0     0        0     0      0   0     0    0      x
0 0      0     0        0     0      0   1     0    0      x
0 0      0     0        0     0      0   0     0    0      x
0 0      0     0        0     0      0   1     0    0      x
0 0      0     0        0     0      0   0     0    0      x
0 0      0     0        0     0      0   1     0    0      x
0 0      0     0        0     0      0   0     0    0      x
0 0      0     0        0     0      0   1     0    0      x
0 0      0     0        0     0      0   0     0    0      x
0 0      0     0        0     0      0   1     0    0      x
0 0      0     0        0     0      0   0     0    0      x
0 0      0     0        0     0      0   1     0    0      x
0 0      0     0        0     0      0   0     0    0      x
0 0      0     0        0     0      0   1     0    0      x
0 0    271     0        1     0      0   0     0    0      x
0 0    271     0        1     0      0   1     0    0      x
0 0    565     0        1     0      0   0     0    0      x
0 0    565     0        1     0      0   1     0    0      x
0 0   8192     0        1     0      0   0     0    0      x
0 0   8192     0        1     0      0   1     0    0      x
0 0   4355     0        1     0      0   0     0    0      x
0 0   4355     0        1     0      0   1     0    0      x
0 0  16128     0        1     0      0   0     0    0      x
0 0  16128     0        1     0      0   1     0    0      x
0 0      0     0        0     1      0   0     0    0      x
0 0      0     0        0     1      0   1     0    0      x
0 0      0     0        0     0      0   0     x    0      x
0 0      0     0        0     0      0   1     x    0      x
0 0      0     0        0     0      0   0     x    0      x
0 0      0     0        0     0      0   1     x    0      x
0 0      0     0        0     0      0   0     x    0      x
0 0      0     0        0     0      0   1     x    0      x
0 0      0     0        0     0      0   0     x    0      x
0 0      0     0        0     0      0   1     x    0      x
0 0      0     0        0     0      0   0     x    0      x
0 0      0     0        0     0      0   1     x    0      x
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*/

/* Test case 06_P04T01:
M N progIn reset progLoad start result clk valid done output
0 0      0     0        0     0      0   0     x    x      x
0 0      0     0        0     0      0   1     x    x      x
0 0      0     1        0     0      0   0     x    x      x
0 0      0     1        0     0      0   1     0    0      x
0 0      0     0        0     0      0   0     0    0      x
0 0      0     0        0     0      0   1     0    0      x
0 0      0     0        0     0      0   0     0    0      x
0 0      0     0        0     0      0   1     0    0      x
0 0      0     0        0     0      0   0     0    0      x
0 0      0     0        0     0      0   1     0    0      x
0 0      0     0        0     0      0   0     0    0      x
0 0      0     0        0     0      0   1     0    0      x
0 0      0     0        0     0      0   0     0    0      x
0 0      0     0        0     0      0   1     0    0      x
0 0      0     0        0     0      0   0     0    0      x
0 0      0     0        0     0      0   1     0    0      x
0 0      0     0        0     0      0   0     0    0      x
0 0      0     0        0     0      0   1     0    0      x
0 0      0     0        0     0      0   0     0    0      x
0 0      0     0        0     0      0   1     0    0      x
0 0      0     0        0     0      0   0     0    0      x
0 0      0     0        0     0      0   1     0    0      x
0 0      0     0        0     0      0   0     0    0      x
0 0      0     0        0     0      0   1     0    0      x
0 0      0     0        0     0      0   0     0    0      x
0 0      0     0        0     0      0   1     0    0      x
0 0      0     0        0     0      0   0     0    0      x
0 0      0     0        0     0      0   1     0    0      x
0 0      0     0        0     0      0   0     0    0      x
0 0      0     0        0     0      0   1     0    0      x
0 0      0     0        0     0      0   0     0    0      x
0 0      0     0        0     0      0   1     0    0      x
0 0      0     0        0     0      0   0     0    0      x
0 0      0     0        0     0      0   1     0    0      x
0 0      0     0        0     0      0   0     0    0      x
0 0      0     0        0     0      0   1     0    0      x
0 0      0     0        0     0      0   0     0    0      x
0 0      0     0        0     0      0   1     0    0      x
0 0      0     0        0     0      0   0     0    0      x
0 0      0     0        0     0      0   1     0    0      x
0 0      0     0        0     0      0   0     0    0      x
0 0      0     0        0     0      0   1     0    0      x
0 0      0     0        0     0      0   0     0    0      x
0 0      0     0        0     0      0   1     0    0      x
0 0    271     0        1     0      0   0     0    0      x
0 0    271     0        1     0      0   1     0    0      x
0 0  12544     0        1     0      0   0     0    0      x
0 0  12544     0        1     0      0   1     0    0      x
0 0   4864     0        1     0      0   0     0    0      x
0 0   4864     0        1     0      0   1     0    0      x
0 0    257     0        1     0      0   0     0    0      x
0 0    257     0        1     0      0   1     0    0      x
0 0   4867     0        1     0      0   0     0    0      x
0 0   4867     0        1     0      0   1     0    0      x
0 0    455     0        1     0      0   0     0    0      x
0 0    455     0        1     0      0   1     0    0      x
0 0  12544     0        1     0      0   0     0    0      x
0 0  12544     0        1     0      0   1     0    0      x
0 0   4873     0        1     0      0   0     0    0      x
0 0   4873     0        1     0      0   1     0    0      x
0 0   4354     0        1     0      0   0     0    0      x
0 0   4354     0        1     0      0   1     0    0      x
0 0   4355     0        1     0      0   0     0    0      x
0 0   4355     0        1     0      0   1     0    0      x
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*/

/* Test case 11_P07T02:
M N progIn reset progLoad start result clk valid done output
0 0      0     0        0     0      0   0     x    x      x
0 0      0     0        0     0      0   1     x    x      x
0 0      0     1        0     0      0   0     x    x      x
0 0      0     1        0     0      0   1     0    0      x
0 0      0     0        0     0      0   0     0    0      x
0 0      0     0        0     0      0   1     0    0      x
0 0      0     0        0     0      0   0     0    0      x
0 0      0     0        0     0      0   1     0    0      x
0 0      0     0        0     0      0   0     0    0      x
0 0      0     0        0     0      0   1     0    0      x
0 0      0     0        0     0      0   0     0    0      x
0 0      0     0        0     0      0   1     0    0      x
0 0      0     0        0     0      0   0     0    0      x
0 0      0     0        0     0      0   1     0    0      x
0 0      0     0        0     0      0   0     0    0      x
0 0      0     0        0     0      0   1     0    0      x
0 0      0     0        0     0      0   0     0    0      x
0 0      0     0        0     0      0   1     0    0      x
0 0      0     0        0     0      0   0     0    0      x
0 0      0     0        0     0      0   1     0    0      x
0 0      0     0        0     0      0   0     0    0      x
0 0      0     0        0     0      0   1     0    0      x
0 0      0     0        0     0      0   0     0    0      x
0 0      0     0        0     0      0   1     0    0      x
0 0      0     0        0     0      0   0     0    0      x
0 0      0     0        0     0      0   1     0    0      x
0 0      0     0        0     0      0   0     0    0      x
0 0      0     0        0     0      0   1     0    0      x
0 0      0     0        0     0      0   0     0    0      x
0 0      0     0        0     0      0   1     0    0      x
0 0      0     0        0     0      0   0     0    0      x
0 0      0     0        0     0      0   1     0    0      x
0 0      0     0        0     0      0   0     0    0      x
0 0      0     0        0     0      0   1     0    0      x
0 0      0     0        0     0      0   0     0    0      x
0 0      0     0        0     0      0   1     0    0      x
0 0      0     0        0     0      0   0     0    0      x
0 0      0     0        0     0      0   1     0    0      x
0 0      0     0        0     0      0   0     0    0      x
0 0      0     0        0     0      0   1     0    0      x
0 0      0     0        0     0      0   0     0    0      x
0 0      0     0        0     0      0   1     0    0      x
0 0      0     0        0     0      0   0     0    0      x
0 0      0     0        0     0      0   1     0    0      x
0 0    446     0        1     0      0   0     0    0      x
0 0    446     0        1     0      0   1     0    0      x
0 0   4353     0        1     0      0   0     0    0      x
0 0   4353     0        1     0      0   1     0    0      x
0 0    426     0        1     0      0   0     0    0      x
0 0    426     0        1     0      0   1     0    0      x
0 0   4367     0        1     0      0   0     0    0      x
0 0   4367     0        1     0      0   1     0    0      x
0 0  13087     0        1     0      0   0     0    0      x
0 0  13087     0        1     0      0   1     0    0      x
0 0  16128     0        1     0      0   0     0    0      x
0 0  16128     0        1     0      0   1     0    0      x
0 0      0     0        0     0      0   0     0    0      x
0 0      0     0        0     0      0   1     0    0      x
0 0      0     0        0     1      0   0     0    0      x
0 0      0     0        0     1      0   1     0    0      x
0 0      0     0        0     0      0   0     x    0      x
0 0      0     0        0     0      0   1     x    0      x
0 0      0     0        0     0      0   0     x    0      x
0 0      0     0        0     0      0   1     x    0      x
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*/

/* Test case 02_P01T02:
M N progIn reset progLoad start result clk valid done output
0 0      0     0        0     0      0   0     x    x      x
0 0      0     0        0     0      0   1     x    x      x
0 0      0     1        0     0      0   0     x    x      x
0 0      0     1        0     0      0   1     0    0      x
0 0      0     0        0     0      0   0     0    0      x
0 0      0     0        0     0      0   1     0    0      x
0 0      0     0        0     0      0   0     0    0      x
0 0      0     0        0     0      0   1     0    0      x
0 0      0     0        0     0      0   0     0    0      x
0 0      0     0        0     0      0   1     0    0      x
0 0      0     0        0     0      0   0     0    0      x
0 0      0     0        0     0      0   1     0    0      x
0 0      0     0        0     0      0   0     0    0      x
0 0      0     0        0     0      0   1     0    0      x
0 0      0     0        0     0      0   0     0    0      x
0 0      0     0        0     0      0   1     0    0      x
0 0      0     0        0     0      0   0     0    0      x
0 0      0     0        0     0      0   1     0    0      x
0 0      0     0        0     0      0   0     0    0      x
0 0      0     0        0     0      0   1     0    0      x
0 0      0     0        0     0      0   0     0    0      x
0 0      0     0        0     0      0   1     0    0      x
0 0      0     0        0     0      0   0     0    0      x
0 0      0     0        0     0      0   1     0    0      x
0 0      0     0        0     0      0   0     0    0      x
0 0      0     0        0     0      0   1     0    0      x
0 0      0     0        0     0      0   0     0    0      x
0 0      0     0        0     0      0   1     0    0      x
0 0      0     0        0     0      0   0     0    0      x
0 0      0     0        0     0      0   1     0    0      x
0 0      0     0        0     0      0   0     0    0      x
0 0      0     0        0     0      0   1     0    0      x
0 0      0     0        0     0      0   0     0    0      x
0 0      0     0        0     0      0   1     0    0      x
0 0      0     0        0     0      0   0     0    0      x
0 0      0     0        0     0      0   1     0    0      x
0 0      0     0        0     0      0   0     0    0      x
0 0      0     0        0     0      0   1     0    0      x
0 0      0     0        0     0      0   0     0    0      x
0 0      0     0        0     0      0   1     0    0      x
0 0      0     0        0     0      0   0     0    0      x
0 0      0     0        0     0      0   1     0    0      x
0 0    271     0        1     0      0   0     0    0      x
0 0    271     0        1     0      0   1     0    0      x
0 0    565     0        1     0      0   0     0    0      x
0 0    565     0        1     0      0   1     0    0      x
0 0   8192     0        1     0      0   0     0    0      x
0 0   8192     0        1     0      0   1     0    0      x
0 0   4355     0        1     0      0   0     0    0      x
0 0   4355     0        1     0      0   1     0    0      x
0 0  16128     0        1     0      0   0     0    0      x
0 0  16128     0        1     0      0   1     0    0      x
0 0      0     0        0     1      0   0     0    0      x
0 0      0     0        0     1      0   1     0    0      x
0 0      0     0        0     0      0   0     x    0      x
0 0      0     0        0     0      0   1     x    0      x
0 0      0     0        0     0      0   0     x    0      x
0 0      0     0        0     0      0   1     x    0      x
0 0      0     0        0     0      0   0     x    0      x
0 0      0     0        0     0      0   1     x    0      x
0 0      0     0        0     0      0   0     x    0      x
0 0      0     0        0     0      0   1     x    0      x
0 0      0     0        0     0      0   0     x    0      x
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*/

/* Test case 07_P05T01:
M N progIn reset progLoad start result clk valid done output
0 0      0     0        0     0      0   0     x    x      x
0 0      0     0        0     0      0   1     x    x      x
0 0      0     1        0     0      0   0     x    x      x
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*/

/* Test case 12_P08T01:
M N progIn reset progLoad start result clk valid done output
0 0      0     0        0     0      0   0     x    x      x
0 0      0     0        0     0      0   1     x    x      x
0 0      0     1        0     0      0   0     x    x      x
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*/

/* Test case 03_P02T01:
M N progIn reset progLoad start result clk valid done output
0 0      0     0        0     0      0   0     x    x      x
0 0      0     0        0     0      0   1     x    x      x
0 0      0     1        0     0      0   0     x    x      x
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*/

/* Test case 08_P06T01:
M N progIn reset progLoad start result clk valid done output
0 0      0     0        0     0      0   0     x    x      x
0 0      0     0        0     0      0   1     x    x      x
0 0      0     1        0     0      0   0     x    x      x
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*/

/* Test case 13_P08T02:
M N progIn reset progLoad start result clk valid done output
0 0      0     0        0     0      0   0     x    x      x
0 0      0     0        0     0      0   1     x    x      x
0 0      0     1        0     0      0   0     x    x      x
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*/

/* Test case 04_P03T01:
M N progIn reset progLoad start result clk valid done output
0 0      0     0        0     0      0   0     x    x      x
0 0      0     0        0     0      0   1     x    x      x
0 0      0     1        0     0      0   0     x    x      x
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*/

/* Test case 09_P06T02:
M N progIn reset progLoad start result clk valid done output
0 0      0     0        0     0      0   0     x    x      x
0 0      0     0        0     0      0   1     x    x      x
0 0      0     1        0     0      0   0     x    x      x
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*/

/* Test case 14_P09T01:
M N progIn reset progLoad start result clk valid done output
0 0      0     0        0     0      0   0     x    x      x
0 0      0     0        0     0      0   1     x    x      x
0 0      0     1        0     0      0   0     x    x      x
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*/

/* Test case T:
progIn progLoad start clk output
262 1 0 0 0
262 1 0 1 0
515 1 0 0 0
515 1 0 1 0
12800 1 0 0 0
12800 1 0 1 0
4871 1 0 0 0
4871 1 0 1 0
257 1 0 0 0
257 1 0 1 0
12800 1 0 0 0
12800 1 0 1 0
16128 1 0 0 0
16128 1 0 1 0
258 1 0 0 0
258 1 0 1 0
12800 1 0 0 0
12800 1 0 1 0
16128 1 0 0 0
16128 1 0 1 0
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*/

/* Test case 05_P03T02:
M N progIn reset progLoad start result clk valid done output
0 0      0     0        0     0      0   0     x    x      x
0 0      0     0        0     0      0   1     x    x      x
0 0      0     1        0     0      0   0     x    x      x
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*/

/* Test case 10_P07T01:
M N progIn reset progLoad start result clk valid done output
0 0      0     0        0     0      0   0     x    x      x
0 0      0     0        0     0      0   1     x    x      x
0 0      0     1        0     0      0   0     x    x      x
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*/

/* Test case 15_P09T02:
M N progIn reset progLoad start result clk valid done output
0 0      0     0        0     0      0   0     x    x      x
0 0      0     0        0     0      0   1     x    x      x
0 0      0     1        0     0      0   0     x    x      x
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*/

/* Test case 26_P10T01:
M N progIn reset progLoad start result clk valid done output
0 0      0     0        0     0      0   0     x    x      x
0 0      0     0        0     0      0   1     x    x      x
0 0      0     1        0     0      0   0     x    x      x
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*/

/* Test case 28_P11T01:
M N progIn reset progLoad start result clk valid done output
0 0      0     0        0     0      0   0     x    x      x
0 0      0     0        0     0      0   1     x    x      x
0 0      0     1        0     0      0   0     x    x      x
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*/

/* Test case Test:
start progLoad progIn clk output
0 1 0x0104 0 x
0 1 0x0104 1 x
0 1 0x3400 0 x
0 1 0x3400 1 x
0 1 0x3F00 0 x
0 1 0x3F00 1 x
0 0 0 0 x
1 0 0 0 x
*/
